// Logisim project DDCO_project.circ as structural Verilog: 9 circuits, main circuit main
module main (
  input  B7,
  input  B6,
  input  B5,
  input  B4,
  input  B3,
  input  B2,
  input  B1,
  input  B0,
  input  A7,
  input  A6,
  input  A5,
  input  A4,
  input  A3,
  input  A2,
  input  A1,
  input  A0,
  input  Cin,
  input  A_nA,
  input  B_n0,
  input  B_nB,
  input  _1_nCin,
  input  R_nL,
  input  SHIFT_nLE_star,
  input  ROTATE,
  input  nCLC,
  output V,
  output N,
  output Z,
  output C,
  output Q7,
  output Q6,
  output Q5,
  output Q4,
  output Q3,
  output Q2,
  output Q1,
  output Q0
);

  wire ADDER_out_22, ADDER_out_23, ADDER_out_24, ADDER_out_25, ADDER_out_26, ADDER_out_27, ADDER_out_28,
       ADDER_out_29, ADDER_out_30, and_1_out, CARRY_SELECT_out_3, CK_out, MUX1_out_10, MUX1_out_11,
       MUX1_out_12, MUX1_out_13, MUX1_out_14, MUX1_out_15, MUX1_out_16, MUX1_out_17, MUX2_out_10,
       MUX2_out_11, MUX2_out_12, MUX2_out_13, MUX2_out_14, MUX2_out_15, MUX2_out_16, MUX2_out_17,
       MUX3_out_10, MUX3_out_11, MUX3_out_12, MUX3_out_13, MUX3_out_14, MUX3_out_15, MUX3_out_16,
       MUX3_out_17, not_1_out, not_2_out, or_1_out, rotates_1_out_4;

  Hex_Digit_Display hex_digit_display_1 (.value({B7, B6, B5, B4}));  // open: dp
  Hex_Digit_Display hex_digit_display_2 (.value({B3, B2, B1, B0}));  // open: dp
  MUX2 MUX2 (
    .in_1(B0), .in_2(B1), .in_3(B2), .in_4(B3), .in_5(B4), .in_6(B5), .in_7(B6), .in_8(B7), .in_9(B_n0),
    .out_10(MUX2_out_10), .out_11(MUX2_out_11), .out_12(MUX2_out_12), .out_13(MUX2_out_13),
    .out_14(MUX2_out_14), .out_15(MUX2_out_15), .out_16(MUX2_out_16), .out_17(MUX2_out_17));
  MUX1 MUX3 (
    .in_1(MUX2_out_10), .in_2(MUX2_out_11), .in_3(MUX2_out_12), .in_4(MUX2_out_13), .in_5(MUX2_out_14),
    .in_6(MUX2_out_15), .in_7(MUX2_out_16), .in_8(MUX2_out_17), .in_9(B_nB), .out_10(MUX3_out_10),
    .out_11(MUX3_out_11), .out_12(MUX3_out_12), .out_13(MUX3_out_13), .out_14(MUX3_out_14),
    .out_15(MUX3_out_15), .out_16(MUX3_out_16), .out_17(MUX3_out_17));
  not not_1 (not_1_out, A_nA);
  CarryS CARRY_SELECT (.in_1(Cin), .in_2(_1_nCin), .out_3(CARRY_SELECT_out_3));
  Hex_Digit_Display hex_digit_display_3 (.value({A7, A6, A5, A4}));  // open: dp
  Hex_Digit_Display hex_digit_display_4 (.value({A3, A2, A1, A0}));  // open: dp
  MUX1 MUX1 (
    .in_1(A0), .in_2(A1), .in_3(A2), .in_4(A3), .in_5(A4), .in_6(A5), .in_7(A6), .in_8(A7), .in_9(A_nA),
    .out_10(MUX1_out_10), .out_11(MUX1_out_11), .out_12(MUX1_out_12), .out_13(MUX1_out_13),
    .out_14(MUX1_out_14), .out_15(MUX1_out_15), .out_16(MUX1_out_16), .out_17(MUX1_out_17));
  Adder ADDER (
    .in_1(CK_out), .in_2(MUX1_out_10), .in_3(MUX1_out_11), .in_4(MUX1_out_12), .in_5(MUX1_out_13),
    .in_6(MUX1_out_14), .in_7(MUX1_out_15), .in_8(MUX1_out_16), .in_9(MUX1_out_17), .in_10(MUX3_out_10),
    .in_11(MUX3_out_11), .in_12(MUX3_out_12), .in_13(MUX3_out_13), .in_14(MUX3_out_14), .in_15(MUX3_out_15),
    .in_16(MUX3_out_16), .in_17(MUX3_out_17), .out_19(V), .out_20(N), .out_21(Z), .out_22(ADDER_out_22),
    .Cin(CARRY_SELECT_out_3), .out_23(ADDER_out_23), .out_24(ADDER_out_24), .out_25(ADDER_out_25),
    .out_26(ADDER_out_26), .out_27(ADDER_out_27), .out_28(ADDER_out_28), .out_29(ADDER_out_29),
    .out_30(ADDER_out_30));
  not not_2 (not_2_out, R_nL);
  or or_1 (or_1_out, ADDER_out_22, not_1_out, B_n0, B_nB, CARRY_SELECT_out_3);
  and and_1 (and_1_out, or_1_out, CARRY_SELECT_out_3);
  RotateS rotates_1 (.in_1(C), .in_2(and_1_out), .in_3(ROTATE), .out_4(rotates_1_out_4));
  Shift SHIFT (
    .in_1(rotates_1_out_4), .in_2(ADDER_out_23), .in_3(ADDER_out_24), .in_4(ADDER_out_25),
    .in_5(ADDER_out_26), .in_6(ADDER_out_27), .in_7(ADDER_out_28), .in_8(ADDER_out_29), .in_9(ADDER_out_30),
    .in_10(CK_out), .in_11(not_2_out), .in_12(SHIFT_nLE_star), .in_13(nCLC), .out_14(Q0), .out_15(Q1),
    .out_16(Q2), .out_17(Q3), .out_18(Q4), .out_19(Q5), .out_20(Q6), .out_21(Q7), .out_22(C));
  Clock CK (.out(CK_out));
  Hex_Digit_Display hex_digit_display_5 (.value({Q7, Q6, Q5, Q4}));  // open: dp
  Hex_Digit_Display hex_digit_display_6 (.value({Q3, Q2, Q1, Q0}));  // open: dp

  // Notes on the sheet:
  //   DATA INPUT B
  //   CONTROL WORDS
  //   ADD + CARRY (A+B+Cin) = 11100001
  //   SUBTRACT (A-B)               = 11010001
  //   NEGATE (2s Comp)           = 00110001
  //   INCREMENT (A+1)             = 10110001
  //   DECREMENT (A-1)             = 11000001
  //   SHIFT LEFT (with carry)    = 10100101
  //   ROTATE LEFT (with carry)  = 11100111
  //   ROTATE RIGHT                    = 11101110
  //   DATA INPUT A
  //   STATUS FLAGS
  //   V = Overflow
  //   N = Negative Result
  //   Z = Zero Result
  //   C = Carry = 1
  //   CARRY LOGIC
  //   ROTATE MODE SELECT
  //   BASIC ALU
  //   RESULT (2's complement notation)
endmodule

module MUX1 (
  input  in_1,
  input  in_2,
  input  in_3,
  input  in_4,
  input  in_5,
  input  in_6,
  input  in_7,
  input  in_8,
  input  in_9,
  output out_10,
  output out_11,
  output out_12,
  output out_13,
  output out_14,
  output out_15,
  output out_16,
  output out_17
);

  wire and_1_out, and_2_out, and_3_out, and_4_out, and_5_out, and_6_out, and_7_out, and_8_out, and_9_out,
       and_10_out, and_11_out, and_12_out, and_13_out, and_14_out, and_15_out, and_16_out, not_1_out,
       not_2_out, not_3_out, not_4_out, not_5_out, not_6_out, not_7_out, not_8_out, not_9_out;

  not not_1 (not_1_out, in_1);
  not not_2 (not_2_out, in_2);
  not not_3 (not_3_out, in_3);
  not not_4 (not_4_out, in_4);
  not not_5 (not_5_out, in_5);
  not not_6 (not_6_out, in_6);
  not not_7 (not_7_out, in_7);
  not not_8 (not_8_out, in_8);
  not not_9 (not_9_out, in_9);
  and and_1 (and_1_out, not_1_out, not_9_out);
  and and_2 (and_2_out, in_1, in_9);
  and and_3 (and_3_out, not_2_out, not_9_out);
  and and_4 (and_4_out, in_2, in_9);
  and and_5 (and_5_out, not_3_out, not_9_out);
  and and_6 (and_6_out, in_3, in_9);
  and and_7 (and_7_out, not_4_out, not_9_out);
  and and_8 (and_8_out, in_4, in_9);
  and and_9 (and_9_out, not_5_out, not_9_out);
  and and_10 (and_10_out, in_5, in_9);
  and and_11 (and_11_out, not_6_out, not_9_out);
  and and_12 (and_12_out, in_6, in_9);
  and and_13 (and_13_out, not_7_out, not_9_out);
  and and_14 (and_14_out, in_7, in_9);
  and and_15 (and_15_out, not_8_out, not_9_out);
  and and_16 (and_16_out, in_8, in_9);
  or or_1 (out_10, and_1_out, and_2_out);
  or or_2 (out_11, and_3_out, and_4_out);
  or or_3 (out_12, and_5_out, and_6_out);
  or or_4 (out_13, and_7_out, and_8_out);
  or or_5 (out_14, and_9_out, and_10_out);
  or or_6 (out_15, and_11_out, and_12_out);
  or or_7 (out_16, and_13_out, and_14_out);
  or or_8 (out_17, and_15_out, and_16_out);
endmodule

module MUX2 (
  input  in_1,
  input  in_2,
  input  in_3,
  input  in_4,
  input  in_5,
  input  in_6,
  input  in_7,
  input  in_8,
  input  in_9,
  output out_10,
  output out_11,
  output out_12,
  output out_13,
  output out_14,
  output out_15,
  output out_16,
  output out_17
);

  wire and_1_out, and_2_out, and_3_out, and_4_out, and_5_out, and_6_out, and_7_out, and_8_out, and_9_out,
       and_10_out, and_11_out, and_12_out, and_13_out, and_14_out, and_15_out, and_16_out, not_1_out;

  not not_1 (not_1_out, in_9);
  and and_1 (and_1_out, 1'b0, not_1_out);
  and and_2 (and_2_out, in_1, in_9);
  and and_3 (and_3_out, 1'b0, not_1_out);
  and and_4 (and_4_out, in_2, in_9);
  and and_5 (and_5_out, 1'b0, not_1_out);
  and and_6 (and_6_out, in_3, in_9);
  and and_7 (and_7_out, 1'b0, not_1_out);
  and and_8 (and_8_out, in_4, in_9);
  and and_9 (and_9_out, 1'b0, not_1_out);
  and and_10 (and_10_out, in_5, in_9);
  and and_11 (and_11_out, 1'b0, not_1_out);
  and and_12 (and_12_out, in_6, in_9);
  and and_13 (and_13_out, 1'b0, not_1_out);
  and and_14 (and_14_out, in_7, in_9);
  and and_15 (and_15_out, 1'b0, not_1_out);
  and and_16 (and_16_out, in_9, in_8);
  or or_1 (out_10, and_1_out, and_2_out);
  or or_2 (out_11, and_3_out, and_4_out);
  or or_3 (out_12, and_5_out, and_6_out);
  or or_4 (out_13, and_7_out, and_8_out);
  or or_5 (out_14, and_9_out, and_10_out);
  or or_6 (out_15, and_11_out, and_12_out);
  or or_7 (out_16, and_13_out, and_14_out);
  or or_8 (out_17, and_15_out, and_16_out);
endmodule

module Adder (
  input  in_1,
  input  in_2,
  input  in_3,
  input  in_4,
  input  in_5,
  input  in_6,
  input  in_7,
  input  in_8,
  input  in_9,
  input  in_10,
  input  in_11,
  input  in_12,
  input  in_13,
  input  in_14,
  input  in_15,
  input  in_16,
  input  in_17,
  input  Cin,
  output out_19,
  output out_20,
  output out_21,
  output out_22,
  output out_23,
  output out_24,
  output out_25,
  output out_26,
  output out_27,
  output out_28,
  output out_29,
  output out_30
);

  wire adder_1_cout, adder_2_cout, adder_3_cout, adder_4_cout, adder_5_cout, adder_6_cout, adder_7_cout,
       adder_8_cout, nor_1_out, xor_1_out;

  D_Flip_Flop d_ff_1 (.clk(in_1), .D(xor_1_out), .Q(out_19), .preset(1'b0), .en(1'b1), .reset(1'b0));  // open: Qn
  Adder_part #(.width(1)) adder_1 (.a(in_2), .b(in_10), .out(out_23), .cin(Cin), .cout(adder_1_cout));
  Adder_part #(.width(1)) adder_2 (.a(in_3), .b(in_11), .out(out_24), .cin(adder_1_cout), .cout(adder_2_cout));
  Adder_part #(.width(1)) adder_3 (.a(in_4), .b(in_12), .out(out_25), .cin(adder_2_cout), .cout(adder_3_cout));
  Adder_part #(.width(1)) adder_4 (.a(in_5), .b(in_13), .out(out_26), .cin(adder_3_cout), .cout(adder_4_cout));
  Adder_part #(.width(1)) adder_5 (.a(in_6), .b(in_14), .out(out_27), .cin(adder_4_cout), .cout(adder_5_cout));
  Adder_part #(.width(1)) adder_6 (.a(in_7), .b(in_15), .out(out_28), .cin(adder_5_cout), .cout(adder_6_cout));
  Adder_part #(.width(1)) adder_7 (.a(in_8), .b(in_16), .out(out_29), .cin(adder_6_cout), .cout(adder_7_cout));
  Adder_part #(.width(1)) adder_8 (.a(in_9), .b(in_17), .out(out_30), .cin(adder_7_cout), .cout(adder_8_cout));
  D_Flip_Flop d_ff_2 (.clk(in_1), .D(out_30), .Q(out_20), .preset(1'b0), .en(1'b1), .reset(1'b0));  // open: Qn
  xor xor_1 (xor_1_out, adder_7_cout, adder_8_cout);
  D_Flip_Flop d_ff_3 (.clk(in_1), .D(nor_1_out), .Q(out_21), .preset(1'b0), .en(1'b1), .reset(1'b0));  // open: Qn
  nor nor_1 (nor_1_out, out_23, out_24, out_25, out_26, out_27, out_28, out_29, out_30);
  D_Flip_Flop d_ff_4 (.clk(in_1), .D(adder_8_cout), .Q(out_22), .preset(1'b0), .en(1'b1), .reset(1'b0));  // open: Qn
endmodule

module Shift (
  input  in_1,
  input  in_2,
  input  in_3,
  input  in_4,
  input  in_5,
  input  in_6,
  input  in_7,
  input  in_8,
  input  in_9,
  input  in_10,
  input  in_11,
  input  in_12,
  input  in_13,
  output out_14,
  output out_15,
  output out_16,
  output out_17,
  output out_18,
  output out_19,
  output out_20,
  output out_21,
  output out_22
);

  wire nand_1_out, not_1_out, s1_1_out_14, s1_1_out_15, s1_2_out_14, s1_2_out_15;

  S1 s1_1 (
    .out_14(s1_1_out_14), .in_1(in_11), .in_2(in_1), .in_4(in_10), .in_5(nand_1_out), .out_10(out_14),
    .out_11(out_15), .out_12(out_16), .out_13(out_17), .in_6(in_2), .in_7(in_3), .in_8(in_4), .in_9(in_5),
    .out_15(s1_1_out_15), .in_3(s1_2_out_14));
  nand nand_1 (nand_1_out, in_10, not_1_out);
  not not_1 (not_1_out, in_12);
  S1 s1_2 (
    .out_14(s1_2_out_14), .in_1(in_11), .in_2(s1_1_out_15), .in_4(in_10), .in_5(nand_1_out), .out_10(out_18),
    .out_11(out_19), .out_12(out_20), .out_13(out_21), .in_6(in_6), .in_7(in_7), .in_8(in_8), .in_9(in_9),
    .out_15(s1_2_out_15), .in_3(s1_1_out_14));
  S2 s2_1 (.in_1(s1_2_out_15), .in_2(in_10), .in_3(in_13), .out_4(out_22));
endmodule

module CarryS (
  input  in_1,
  input  in_2,
  output out_3
);

  wire nand_1_out, nand_2_out, not_1_out;

  not not_1 (not_1_out, in_2);
  nand nand_1 (nand_1_out, in_2, 1'b1);
  nand nand_2 (nand_2_out, not_1_out, in_1);
  nand nand_3 (out_3, nand_1_out, nand_2_out);
endmodule

module RotateS (
  input  in_1,
  input  in_2,
  input  in_3,
  output out_4
);

  wire nand_1_out, nand_2_out, not_1_out;

  not not_1 (not_1_out, in_3);
  nand nand_1 (nand_1_out, in_3, in_1);
  nand nand_2 (nand_2_out, not_1_out, in_2);
  nand nand_3 (out_4, nand_1_out, nand_2_out);
endmodule

module S1 (
  input  in_1,
  input  in_2,
  input  in_3,
  input  in_4,
  input  in_5,
  input  in_6,
  input  in_7,
  input  in_8,
  input  in_9,
  output out_10,
  output out_11,
  output out_12,
  output out_13,
  output out_14,
  output out_15
);

  wire and_1_out, and_2_out, and_3_out, and_4_out, and_5_out, and_6_out, and_7_out, and_8_out, and_9_out,
       and_10_out, and_11_out, and_12_out, j_k_ff_1_qn, j_k_ff_2_qn, j_k_ff_3_qn, j_k_ff_4_qn, nand_1_out,
       nand_2_out, nand_3_out, nand_4_out, nand_5_out, nand_6_out, nand_7_out, nand_8_out, not_1_out,
       not_2_out, not_3_out, not_4_out, not_5_out, not_6_out, not_7_out, not_8_out, not_9_out, not_10_out,
       not_11_out, not_12_out;

  not not_1 (not_1_out, in_2);
  not not_2 (not_2_out, in_1);
  nand nand_1 (nand_1_out, not_1_out, in_1);
  and and_1 (and_1_out, nand_1_out, nand_2_out);
  not not_3 (not_3_out, in_5);
  nand nand_2 (nand_2_out, not_2_out, j_k_ff_2_qn);
  J_K_Flip_Flop j_k_ff_1 (
    .J(and_1_out), .clk(in_4), .K(not_4_out), .Q(out_10), .Qn(j_k_ff_1_qn), .preset(and_2_out), .en(1'b1),
    .reset(and_3_out));
  not not_4 (not_4_out, and_1_out);
  and and_2 (and_2_out, not_3_out, in_6);
  not not_5 (not_5_out, in_6);
  and and_3 (and_3_out, not_3_out, not_5_out);
  nand nand_3 (nand_3_out, j_k_ff_1_qn, in_1);
  nand nand_4 (nand_4_out, not_2_out, j_k_ff_3_qn);
  and and_4 (and_4_out, nand_3_out, nand_4_out);
  J_K_Flip_Flop j_k_ff_2 (
    .J(and_4_out), .clk(in_4), .K(not_6_out), .Q(out_11), .Qn(j_k_ff_2_qn), .preset(and_5_out), .en(1'b1),
    .reset(and_6_out));
  not not_6 (not_6_out, and_4_out);
  and and_5 (and_5_out, not_3_out, in_7);
  and and_6 (and_6_out, not_3_out, not_7_out);
  not not_7 (not_7_out, in_7);
  nand nand_5 (nand_5_out, j_k_ff_2_qn, in_1);
  nand nand_6 (nand_6_out, not_2_out, j_k_ff_4_qn);
  and and_7 (and_7_out, nand_5_out, nand_6_out);
  not not_8 (not_8_out, and_7_out);
  and and_8 (and_8_out, not_3_out, in_8);
  J_K_Flip_Flop j_k_ff_3 (
    .J(and_7_out), .clk(in_4), .K(not_8_out), .Q(out_12), .Qn(j_k_ff_3_qn), .preset(and_8_out), .en(1'b1),
    .reset(and_9_out));
  and and_9 (and_9_out, not_3_out, not_9_out);
  not not_9 (not_9_out, in_8);
  nand nand_7 (nand_7_out, j_k_ff_3_qn, in_1);
  nand nand_8 (nand_8_out, not_2_out, not_11_out);
  and and_10 (and_10_out, nand_7_out, nand_8_out);
  not not_10 (not_10_out, and_10_out);
  and and_11 (and_11_out, not_3_out, in_9);
  not not_11 (not_11_out, in_3);
  J_K_Flip_Flop j_k_ff_4 (
    .J(and_10_out), .clk(in_4), .K(not_10_out), .Q(out_13), .Qn(j_k_ff_4_qn), .preset(and_11_out), .en(1'b1),
    .reset(and_12_out));
  and and_12 (and_12_out, not_3_out, not_12_out);
  not not_12 (not_12_out, in_9);

  assign out_14 = out_10;
  assign out_15 = out_13;
endmodule

module S2 (
  input  in_1,
  input  in_2,
  input  in_3,
  output out_4
);

  wire not_1_out, not_2_out;

  not not_1 (not_1_out, in_1);
  J_K_Flip_Flop j_k_ff_1 (
    .J(in_1), .clk(in_2), .K(not_1_out), .Q(out_4), .preset(1'b0), .en(1'b1), .reset(not_2_out));  // open: Qn
  not not_2 (not_2_out, in_3);
endmodule
